# Fritzing sketch HardwareSketch (saved by Fritzing 0.9.3b)
breadboards: 1

parts:
  DS1 = DS18B20 1-Wire Temperature Sensor [part_number=DS18B20]
  M1 = ESP32-S2-DevKitC-1 [part_number=ESP32-S2-DevKitC-1]
  R1 = Resistor [tolerance=±5% resistance=220 package=THT]

nets:
  N1: DS1.GND, M1.pin_1, M1.pin_22, M1.pin_44, R1.Pin_0
  N2: DS1.DQ, M1.pin_5, R1.Pin_1

notes:
  Sd kort er indbygget i Esp32-S3-vroom
  // Pin definitions for SD card
  #define SD_MMC_CMD 38 /**< SD card command pin */
  #define SD_MMC_CLK 39 /**< SD card clock pin */
  #define SD_MMC_D0 40 /**< SD card data pin */

custom parts:
  ESP32-S2-DevKitC-1: ESP32-S2-DevKitC-1 is an entry-level development board based on ESP32-S2-SOLO (on-board PCB antenna). It is based on the ESP32 microcontroller that boasts Wifi, Bluetooth, Ethernet and Low Power support all in a single chip. (vanepp) Feb 2022: converted to ESP32-S2-DevKitC-1. This module is 44pins long (2x22) and 11 pins width.
